// Logisim project 8_bits_logic.circ as structural Verilog: 22 circuits, main circuit and2
module and2 (
  input  [1:0] A,
  input  [1:0] B,
  output [1:0] S
);

  and and_1 (S[0], A[0], B[0]);
  and and_2 (S[1], A[1], B[1]);
endmodule

module and4 (
  input  [3:0] A,
  input  [3:0] B,
  output [3:0] S
);

  and2 and2_1 (.A(A[1:0]), .B(B[1:0]), .S(S[1:0]));
  and2 and2_2 (.A(A[3:2]), .B(B[3:2]), .S(S[3:2]));
endmodule

module and8 (
  input  [7:0] A,
  input  [7:0] B,
  output [7:0] S
);

  and4 and4_1 (.A(A[3:0]), .B(B[3:0]), .S(S[3:0]));
  and4 and4_2 (.A(A[7:4]), .B(B[7:4]), .S(S[7:4]));
endmodule

module or2 (
  input  [1:0] A,
  input  [1:0] B,
  output [1:0] S
);

  or or_1 (S[0], A[0], B[0]);
  or or_2 (S[1], A[1], B[1]);
endmodule

module or4 (
  input  [3:0] A,
  input  [3:0] B,
  output [3:0] S
);

  or2 or2_1 (.A(A[1:0]), .B(B[1:0]), .S(S[1:0]));
  or2 or2_2 (.A(A[3:2]), .B(B[3:2]), .S(S[3:2]));
endmodule

module or8 (
  input  [7:0] A,
  input  [7:0] B,
  output [7:0] S
);

  or4 or4_1 (.A(A[3:0]), .B(B[3:0]), .S(S[3:0]));
  or4 or4_2 (.A(A[7:4]), .B(B[7:4]), .S(S[7:4]));
endmodule

module nand2 (
  input  [1:0] A,
  input  [1:0] B,
  output [1:0] S
);

  nand nand_1 (S[0], A[0], B[0]);
  nand nand_2 (S[1], A[1], B[1]);
endmodule

module nand4 (
  input  [3:0] A,
  input  [3:0] B,
  output [3:0] S
);

  nand2 nand2_1 (.A(A[1:0]), .B(B[1:0]), .S(S[1:0]));
  nand2 nand2_2 (.A(A[3:2]), .B(B[3:2]), .S(S[3:2]));
endmodule

module nand8 (
  input  [7:0] A,
  input  [7:0] B,
  output [7:0] S
);

  nand4 nand4_1 (.A(A[3:0]), .B(B[3:0]), .S(S[3:0]));
  nand4 nand4_2 (.A(A[7:4]), .B(B[7:4]), .S(S[7:4]));
endmodule

module nor2 (
  input  [1:0] A,
  input  [1:0] B,
  output [1:0] S
);

  nor nor_1 (S[0], A[0], B[0]);
  nor nor_2 (S[1], A[1], B[1]);
endmodule

module nor4 (
  input  [3:0] A,
  input  [3:0] B,
  output [3:0] S
);

  nor2 nor2_1 (.A(A[1:0]), .B(B[1:0]), .S(S[1:0]));
  nor2 nor2_2 (.A(A[3:2]), .B(B[3:2]), .S(S[3:2]));
endmodule

module nor8 (
  input  [7:0] A,
  input  [7:0] B,
  output [7:0] S
);

  nor4 nor4_1 (.A(A[3:0]), .B(B[3:0]), .S(S[3:0]));
  nor4 nor4_2 (.A(A[7:4]), .B(B[7:4]), .S(S[7:4]));
endmodule

module xor2 (
  input  [1:0] A,
  input  [1:0] B,
  output [1:0] S
);

  xor xor_1 (S[0], A[0], B[0]);
  xor xor_2 (S[1], A[1], B[1]);
endmodule

module xor4 (
  input  [3:0] A,
  input  [3:0] B,
  output [3:0] S
);

  xor2 xor2_1 (.A(A[1:0]), .B(B[1:0]), .S(S[1:0]));
  xor2 xor2_2 (.A(A[3:2]), .B(B[3:2]), .S(S[3:2]));
endmodule

module xor8 (
  input  [7:0] A,
  input  [7:0] B,
  output [7:0] S
);

  xor4 xor4_1 (.A(A[3:0]), .B(B[3:0]), .S(S[3:0]));
  xor4 xor4_2 (.A(A[7:4]), .B(B[7:4]), .S(S[7:4]));
endmodule

module nxor2 (
  input  [1:0] A,
  input  [1:0] B,
  output [1:0] S
);

  xnor xnor_1 (S[0], A[0], B[0]);
  xnor xnor_2 (S[1], A[1], B[1]);
endmodule

module nxor4 (
  input  [3:0] A,
  input  [3:0] B,
  output [3:0] S
);

  nxor2 nxor2_1 (.A(A[1:0]), .B(B[1:0]), .S(S[1:0]));
  nxor2 nxor2_2 (.A(A[3:2]), .B(B[3:2]), .S(S[3:2]));
endmodule

module nxor8 (
  input  [7:0] A,
  input  [7:0] B,
  output [7:0] S
);

  nxor4 nxor4_1 (.A(A[3:0]), .B(B[3:0]), .S(S[3:0]));
  nxor4 nxor4_2 (.A(A[7:4]), .B(B[7:4]), .S(S[7:4]));
endmodule

module not2 (
  input  [1:0] A,
  output [1:0] S
);

  not not_1 (S[0], A[0]);
  not not_2 (S[1], A[1]);
endmodule

module not4 (
  input  [3:0] A,
  output [3:0] S
);

  not2 not2_1 (.A(A[1:0]), .S(S[1:0]));
  not2 not2_2 (.A(A[3:2]), .S(S[3:2]));
endmodule

module not8 (
  input  [7:0] A,
  output [7:0] S
);

  not4 not4_1 (.A(A[3:0]), .S(S[3:0]));
  not4 not4_2 (.A(A[7:4]), .S(S[7:4]));
endmodule

module ul_exo1_and_or_xor8 (
  input  [7:0] A,
  input  [7:0] B,
  output [7:0] AND,
  output [7:0] OR,
  output [7:0] XOR
);

  and8 and8_1 (.A(A), .B(B), .S(AND));
  or8 or8_1 (.A(A), .B(B), .S(OR));
  xor8 xor8_1 (.A(A), .B(B), .S(XOR));
endmodule
