// Logisim project maths.circ as structural Verilog: 4 circuits, main circuit add1
module add1 (
  input  A,
  input  B,
  input  CIN,
  output S,
  output COUT
);

  wire and_1_out, and_2_out, xor_1_out;

  and and_1 (and_1_out, B, A);
  or or_1 (COUT, and_1_out, and_2_out);
  xor xor_1 (xor_1_out, A, B);
  and and_2 (and_2_out, CIN, xor_1_out);
  xor xor_2 (S, xor_1_out, CIN);
endmodule

module add2 (
  input  [1:0] A,
  input  [1:0] B,
  input  CIN,
  output [1:0] S,
  output COUT
);

  wire add1_1_cout;

  add1 add1_1 (.A(A[0]), .B(B[0]), .CIN(CIN), .COUT(add1_1_cout), .S(S[0]));
  add1 add1_2 (.A(A[1]), .B(B[1]), .CIN(add1_1_cout), .COUT(COUT), .S(S[1]));
endmodule

module add4 (
  input  [3:0] A,
  input  [3:0] B,
  input  CIN,
  output [3:0] S,
  output COUT
);

  wire add2_1_cout;

  add2 add2_1 (.A(A[1:0]), .B(B[1:0]), .CIN(CIN), .COUT(add2_1_cout), .S(S[1:0]));
  add2 add2_2 (.A(A[3:2]), .B(B[3:2]), .CIN(add2_1_cout), .COUT(COUT), .S(S[3:2]));
endmodule

module add8 (
  input  [7:0] A,
  input  [7:0] B,
  input  CIN,
  output [7:0] S,
  output COUT
);

  wire add4_1_cout;

  add4 add4_1 (.A(A[3:0]), .B(B[3:0]), .CIN(CIN), .COUT(add4_1_cout), .S(S[3:0]));
  add4 add4_2 (.A(A[7:4]), .B(B[7:4]), .CIN(add4_1_cout), .COUT(COUT), .S(S[7:4]));
endmodule
