// Logisim project microproc.circ as structural Verilog: 10 circuits, main circuit microprocesseur
module pc_and_rom (
  input  HORLOGE,
  input  [7:0] NOUVELLE_ADDR,
  input  SET_ADDR,
  output [15:0] INSTRUCTION
);

  wire [7:0] INCR_PC_s, multiplexer_1_out, PC_etat_du_registre;

  Multiplexer #(.width(8), .enable("false")) multiplexer_1 (
    .in0(INCR_PC_s), .in1(NOUVELLE_ADDR), .out(multiplexer_1_out), .sel(SET_ADDR));
  registre8 PC (.ENABLE(1'b1), .HORLOGE(HORLOGE), .ENTREE(multiplexer_1_out), .ETAT_DU_REGISTRE(PC_etat_du_registre));
  add8 INCR_PC (.A(PC_etat_du_registre), .B(8'h1), .CIN(1'b0), .S(INCR_PC_s));  // open: COUT
  ROM #(.dataWidth(16), .Select("low")) ROM_PROGRAMME (.addr(PC_etat_du_registre), .data(INSTRUCTION));

  // Notes on the sheet:
  //   contents of ROM_PROGRAMME (hex, n*v repeats v):
  //   4602 420a 2d40 1560 6402 4c02 40 4602 560 6402 47f6 560 9b00 6000
endmodule

module instr_decode (
  input  [15:0] INSTR,
  output [10:0] PAYLOAD,
  output [2:0] NUM_INSTR,
  output [1:0] WHICH_INSTR_DECODER
);


  assign NUM_INSTR = INSTR[13:11];
  assign PAYLOAD = INSTR[10:0];
  assign WHICH_INSTR_DECODER = INSTR[15:14];
endmodule

module microprocesseur (
);

  wire HORLOGE_out, INSTR_JUMP_DECODER_set_addr, INSTR_LOAD_AND_STORE_DECODER_ram_write;
  wire [1:0] INSTR_DECODE_which_instr_decoder;
  wire [2:0] INSTR_DECODE_num_instr, INSTR_MATH_AND_LOGIC_DECODER_ual_signal;
  wire [6:0] INSTR_JUMP_DECODER_reg_signal, INSTR_LOAD_AND_STORE_DECODER_reg_signal,
       INSTR_MATH_AND_LOGIC_DECODER_reg_signal, WHICH_SIGNAL_reg_signal;
  wire [7:0] BANC_REGISTRES_a, BANC_REGISTRES_b, INSTR_JUMP_DECODER_addr,
       INSTR_LOAD_AND_STORE_DECODER_ram_addr, INSTR_LOAD_AND_STORE_DECODER_ram_store,
       INSTR_LOAD_AND_STORE_DECODER_reg_entry, RAM_loaded, ual_1_s, WHICH_ENTRY_reg_entry;
  wire [10:0] INSTR_DECODE_payload;
  wire [15:0] PC_AND_ROM_instruction;

  Clock HORLOGE (.out(HORLOGE_out));
  pc_and_rom PC_AND_ROM (
    .NOUVELLE_ADDR(INSTR_JUMP_DECODER_addr), .HORLOGE(HORLOGE_out), .SET_ADDR(INSTR_JUMP_DECODER_set_addr),
    .INSTRUCTION(PC_AND_ROM_instruction));
  instr_decode INSTR_DECODE (
    .INSTR(PC_AND_ROM_instruction), .PAYLOAD(INSTR_DECODE_payload), .NUM_INSTR(INSTR_DECODE_num_instr),
    .WHICH_INSTR_DECODER(INSTR_DECODE_which_instr_decoder));
  ram RAM (
    .VALUE(INSTR_LOAD_AND_STORE_DECODER_ram_store), .ADDR(INSTR_LOAD_AND_STORE_DECODER_ram_addr),
    .HORLOGE(HORLOGE_out), .WRITE_ENABLE(INSTR_LOAD_AND_STORE_DECODER_ram_write), .LOADED(RAM_loaded));
  instr_maths_logic INSTR_MATH_AND_LOGIC_DECODER (
    .PAYLOAD(INSTR_DECODE_payload), .NUM_INSTR(INSTR_DECODE_num_instr),
    .REG_SIGNAL(INSTR_MATH_AND_LOGIC_DECODER_reg_signal), .UAL_SIGNAL(INSTR_MATH_AND_LOGIC_DECODER_ual_signal));
  instr_load_and_store INSTR_LOAD_AND_STORE_DECODER (
    .PAYLOAD(INSTR_DECODE_payload), .REG_SIGNAL(INSTR_LOAD_AND_STORE_DECODER_reg_signal),
    .RAM_LOAD(RAM_loaded), .REGB_LOAD(BANC_REGISTRES_b), .RAM_ADDR(INSTR_LOAD_AND_STORE_DECODER_ram_addr),
    .RAM_STORE(INSTR_LOAD_AND_STORE_DECODER_ram_store), .REG_ENTRY(INSTR_LOAD_AND_STORE_DECODER_reg_entry),
    .NUM_INSTR(INSTR_DECODE_num_instr), .RAM_WRITE(INSTR_LOAD_AND_STORE_DECODER_ram_write),
    .REGA_LOAD(BANC_REGISTRES_a), .WHICH_INSTR_DECODER(INSTR_DECODE_which_instr_decoder));
  which_reg_entry WHICH_ENTRY (
    .UAL(ual_1_s), .LOAD(INSTR_LOAD_AND_STORE_DECODER_reg_entry), .WHICH(INSTR_DECODE_which_instr_decoder),
    .REG_ENTRY(WHICH_ENTRY_reg_entry));
  which_reg_signal WHICH_SIGNAL (
    .MATH_AND_LOGIC_SIGNAL(INSTR_MATH_AND_LOGIC_DECODER_reg_signal),
    .LOAD_AND_STORE_SIGNAL(INSTR_LOAD_AND_STORE_DECODER_reg_signal),
    .JUMP_SIGNAL(INSTR_JUMP_DECODER_reg_signal), .WHICH(INSTR_DECODE_which_instr_decoder),
    .REG_SIGNAL(WHICH_SIGNAL_reg_signal));
  instr_jump_decoder INSTR_JUMP_DECODER (
    .WHICH_INSTR(INSTR_DECODE_which_instr_decoder), .REGA(BANC_REGISTRES_a), .REGB(BANC_REGISTRES_b),
    .PAYLOAD(INSTR_DECODE_payload), .REG_SIGNAL(INSTR_JUMP_DECODER_reg_signal),
    .NUM_INSTR(INSTR_DECODE_num_instr), .SET_ADDR(INSTR_JUMP_DECODER_set_addr), .ADDR(INSTR_JUMP_DECODER_addr));
  banc_registres8 BANC_REGISTRES (
    .E(WHICH_ENTRY_reg_entry), .SIGNAL(WHICH_SIGNAL_reg_signal), .HORLOGE(HORLOGE_out), .A(BANC_REGISTRES_a),
    .B(BANC_REGISTRES_b));
  ual ual_1 (
    .A(BANC_REGISTRES_a), .B(BANC_REGISTRES_b), .S(ual_1_s),
    .OP_A_EFFECTUER(INSTR_MATH_AND_LOGIC_DECODER_ual_signal));  // open: CARRY_FLAG
endmodule

module instr_load_and_store (
  input  [1:0] WHICH_INSTR_DECODER,
  input  [2:0] NUM_INSTR,
  input  [10:0] PAYLOAD,
  input  [7:0] RAM_LOAD,
  input  [7:0] REGA_LOAD,
  input  [7:0] REGB_LOAD,
  output [6:0] REG_SIGNAL,
  output RAM_WRITE,
  output [7:0] REG_ENTRY,
  output [7:0] RAM_STORE,
  output [7:0] RAM_ADDR
);

  wire not_1_out;

  Multiplexer #(.width(8), .enable("false")) multiplexer_1 (
    .in0(PAYLOAD[8:1]), .in1(REGA_LOAD), .out(RAM_ADDR), .sel(NUM_INSTR[1]));
  Multiplexer #(.select(2), .width(8), .enable("false")) multiplexer_2 (
    .in0(PAYLOAD[8:1]), .in1(RAM_LOAD), .in2(REGB_LOAD), .in3(REGB_LOAD), .out(REG_ENTRY),
    .sel(NUM_INSTR[1:0]));
  Multiplexer #(.select(3), .width(7), .enable("false")) multiplexer_3 (
    .in0({1'b1, PAYLOAD[10:7], 2'b00}), .in1({1'b1, PAYLOAD[10:7], 2'b00}),
    .in2({1'b1, PAYLOAD[10:7], 2'b00}), .in3({3'b000, PAYLOAD[8:7], PAYLOAD[10:9]}),
    .in4({3'b000, PAYLOAD[10:9], 2'b00}), .in5({3'b000, PAYLOAD[10:9], 2'b00}),
    .in6({3'b000, PAYLOAD[10:9], 2'b00}), .in7({3'b000, PAYLOAD[10:9], 2'b00}), .out(REG_SIGNAL),
    .sel(NUM_INSTR));
  not not_1 (not_1_out, REG_SIGNAL[6]);
  and and_1 (RAM_WRITE, not_1_out, WHICH_INSTR_DECODER[0]);

  assign RAM_STORE = REGB_LOAD;
endmodule

module instr_maths_logic (
  input  [10:0] PAYLOAD,
  input  [2:0] NUM_INSTR,
  output [6:0] REG_SIGNAL,
  output [2:0] UAL_SIGNAL
);


  assign REG_SIGNAL = {1'b1, PAYLOAD[10:5]};
  assign UAL_SIGNAL = NUM_INSTR;
endmodule

module ram (
  input  [7:0] VALUE,
  input  [7:0] ADDR,
  input  HORLOGE,
  input  WRITE_ENABLE,
  output [7:0] LOADED
);

  wire not_1_out;

  assign LOADED = ~not_1_out ? VALUE : 8'bz;  // Controlled_Buffer controlled_buffer_1
  not not_1 (not_1_out, WRITE_ENABLE);
  RAM #(.simpleMode("false"), .Select("low")) RAM (
    .addr(ADDR), .data(LOADED), .clk(HORLOGE), .ld(not_1_out));  // open: sel, clr
endmodule

module which_reg_signal (
  input  [6:0] MATH_AND_LOGIC_SIGNAL,
  input  [6:0] LOAD_AND_STORE_SIGNAL,
  input  [6:0] JUMP_SIGNAL,
  input  [1:0] WHICH,
  output [6:0] REG_SIGNAL
);

  Multiplexer #(.select(2), .width(7), .enable("false")) multiplexer_1 (
    .in0(MATH_AND_LOGIC_SIGNAL), .in1(LOAD_AND_STORE_SIGNAL), .in2(JUMP_SIGNAL), .in3({7{1'b0}}),
    .out(REG_SIGNAL), .sel(WHICH));
endmodule

module which_reg_entry (
  input  [7:0] UAL,
  input  [7:0] LOAD,
  input  [1:0] WHICH,
  output [7:0] REG_ENTRY
);

  Multiplexer #(.width(8), .enable("false")) multiplexer_1 (.in0(UAL), .in1(LOAD), .out(REG_ENTRY), .sel(WHICH[0]));
endmodule

module instr_jump_decoder (
  input  [1:0] WHICH_INSTR,
  input  [7:0] REGA,
  input  [7:0] REGB,
  input  [10:0] PAYLOAD,
  input  [2:0] NUM_INSTR,
  output [7:0] ADDR,
  output SET_ADDR,
  output [6:0] REG_SIGNAL
);

  wire and_1_out, and_2_out, is_zero_1_is_zero, not_1_out, not_2_out, not_3_out, or_1_out, or_2_out;

  Multiplexer #(.select(2), .width(7), .enable("false")) multiplexer_1 (
    .in0({7{1'b0}}), .in1({3'b000, PAYLOAD[10:7]}), .in2({3'b000, PAYLOAD[10:7]}),
    .in3({3'b000, PAYLOAD[10:7]}), .out(REG_SIGNAL), .sel(NUM_INSTR[1:0]));
  is_zero is_zero_1 (.INPUT(REGA), .IS_ZERO(is_zero_1_is_zero));
  not not_1 (not_1_out, NUM_INSTR[0]);
  not not_2 (not_2_out, is_zero_1_is_zero);
  not not_3 (not_3_out, NUM_INSTR[1]);
  Multiplexer #(.select(2), .width(8), .enable("false")) multiplexer_2 (
    .in0(PAYLOAD[10:3]), .in1(REGB), .in2(REGB), .in3(REGB), .out(ADDR), .sel(NUM_INSTR[1:0]));
  and and_1 (and_1_out, is_zero_1_is_zero, not_1_out);
  or or_1 (or_1_out, and_1_out, and_2_out);
  and and_2 (and_2_out, not_2_out, NUM_INSTR[0]);
  or or_2 (or_2_out, not_3_out, or_1_out);
  and and_3 (SET_ADDR, or_2_out, WHICH_INSTR[1]);
endmodule

module is_zero (
  input  [7:0] INPUT,
  output IS_ZERO
);

  wire or_1_out, or_2_out, or_3_out, or_4_out, or_5_out, or_6_out, or_7_out;

  or or_1 (or_1_out, INPUT[1], INPUT[3]);
  or or_2 (or_2_out, INPUT[4], INPUT[6]);
  or or_3 (or_3_out, INPUT[0], INPUT[2]);
  or or_4 (or_4_out, INPUT[5], INPUT[7]);
  or or_5 (or_5_out, or_1_out, or_3_out);
  or or_6 (or_6_out, or_5_out, or_7_out);
  or or_7 (or_7_out, or_4_out, or_2_out);
  not not_1 (IS_ZERO, or_6_out);
endmodule
