// Logisim project registres.circ as structural Verilog: 3 circuits, main circuit registre8
module registre8 (
  input  ENABLE,
  input  HORLOGE,
  input  [7:0] ENTREE,
  output [7:0] ETAT_DU_REGISTRE
);

  D_Flip_Flop #(.enable("true")) d_ff_1 (
    .clk(HORLOGE), .D(ENTREE[0]), .Q(ETAT_DU_REGISTRE[0]), .en(ENABLE));  // open: Qn, preset, reset
  D_Flip_Flop #(.enable("true")) d_ff_2 (
    .clk(HORLOGE), .D(ENTREE[1]), .Q(ETAT_DU_REGISTRE[1]), .en(ENABLE));  // open: Qn, preset, reset
  D_Flip_Flop #(.enable("true")) d_ff_3 (
    .clk(HORLOGE), .D(ENTREE[2]), .Q(ETAT_DU_REGISTRE[2]), .en(ENABLE));  // open: Qn, preset, reset
  D_Flip_Flop #(.enable("true")) d_ff_4 (
    .clk(HORLOGE), .D(ENTREE[3]), .Q(ETAT_DU_REGISTRE[3]), .en(ENABLE));  // open: Qn, preset, reset
  D_Flip_Flop #(.enable("true")) d_ff_5 (
    .clk(HORLOGE), .D(ENTREE[4]), .Q(ETAT_DU_REGISTRE[4]), .en(ENABLE));  // open: Qn, preset, reset
  D_Flip_Flop #(.enable("true")) d_ff_6 (
    .clk(HORLOGE), .D(ENTREE[5]), .Q(ETAT_DU_REGISTRE[5]), .en(ENABLE));  // open: Qn, preset, reset
  D_Flip_Flop #(.enable("true")) d_ff_7 (
    .clk(HORLOGE), .D(ENTREE[6]), .Q(ETAT_DU_REGISTRE[6]), .en(ENABLE));  // open: Qn, preset, reset
  D_Flip_Flop #(.enable("true")) d_ff_8 (
    .clk(HORLOGE), .D(ENTREE[7]), .Q(ETAT_DU_REGISTRE[7]), .en(ENABLE));  // open: Qn, preset, reset
endmodule

module banc_registres8 (
  input  [7:0] E,
  input  [6:0] SIGNAL,
  input  HORLOGE,
  output [7:0] A,
  output [7:0] B
);

  wire demultiplexer_1_out0, demultiplexer_1_out1, demultiplexer_1_out2, demultiplexer_1_out3;
  wire [7:0] R1_etat_du_registre, R2_etat_du_registre, R3_etat_du_registre, R4_etat_du_registre;

  Demultiplexer #(.select(2), .enable("false")) demultiplexer_1 (
    .out0(demultiplexer_1_out0), .out1(demultiplexer_1_out1), .out2(demultiplexer_1_out2),
    .out3(demultiplexer_1_out3), .in(SIGNAL[6]), .sel(SIGNAL[5:4]));
  registre8 R1 (.ENABLE(demultiplexer_1_out0), .HORLOGE(HORLOGE), .ENTREE(E), .ETAT_DU_REGISTRE(R1_etat_du_registre));
  registre8 R2 (.ENABLE(demultiplexer_1_out1), .HORLOGE(HORLOGE), .ENTREE(E), .ETAT_DU_REGISTRE(R2_etat_du_registre));
  registre8 R3 (.ENABLE(demultiplexer_1_out2), .HORLOGE(HORLOGE), .ENTREE(E), .ETAT_DU_REGISTRE(R3_etat_du_registre));
  registre8 R4 (.ENABLE(demultiplexer_1_out3), .HORLOGE(HORLOGE), .ENTREE(E), .ETAT_DU_REGISTRE(R4_etat_du_registre));
  Multiplexer #(.select(2), .width(8), .enable("false")) multiplexer_1 (
    .in0(R1_etat_du_registre), .in1(R2_etat_du_registre), .in2(R3_etat_du_registre),
    .in3(R4_etat_du_registre), .out(A), .sel(SIGNAL[1:0]));
  Multiplexer #(.select(2), .width(8), .enable("false")) multiplexer_2 (
    .in0(R1_etat_du_registre), .in1(R2_etat_du_registre), .in2(R3_etat_du_registre),
    .in3(R4_etat_du_registre), .out(B), .sel(SIGNAL[3:2]));
endmodule

module ual_plus_reg (
  input  [6:0] SIGNAL,
  input  [2:0] OPERATION,
  output out_3
);

  wire clock_1_out;
  wire [7:0] banc_registres8_1_a, banc_registres8_1_b, ual_1_s;

  Clock clock_1 (.out(clock_1_out));
  banc_registres8 banc_registres8_1 (
    .E(ual_1_s), .SIGNAL(SIGNAL), .HORLOGE(clock_1_out), .A(banc_registres8_1_a), .B(banc_registres8_1_b));
  ual ual_1 (
    .A(banc_registres8_1_a), .B(banc_registres8_1_b), .S(ual_1_s), .OP_A_EFFECTUER(OPERATION),
    .CARRY_FLAG(out_3));
endmodule
