// Logisim project ual.circ as structural Verilog: 1 circuit, main circuit ual
module ual (
  input  [7:0] A,
  input  [7:0] B,
  input  [2:0] OP_A_EFFECTUER,
  output CARRY_FLAG,
  output [7:0] S
);

  wire [7:0] add8_1_s, and8_1_s, nand8_1_s, nor8_1_s, not8_1_s, nxor8_1_s, or8_1_s, xor8_1_s;

  add8 add8_1 (.A(A), .B(B), .CIN(1'b0), .COUT(CARRY_FLAG), .S(add8_1_s));
  and8 and8_1 (.A(A), .B(B), .S(and8_1_s));
  or8 or8_1 (.A(A), .B(B), .S(or8_1_s));
  nand8 nand8_1 (.A(A), .B(B), .S(nand8_1_s));
  nor8 nor8_1 (.A(A), .B(B), .S(nor8_1_s));
  xor8 xor8_1 (.A(A), .B(B), .S(xor8_1_s));
  nxor8 nxor8_1 (.A(A), .B(B), .S(nxor8_1_s));
  not8 not8_1 (.A(B), .S(not8_1_s));
  Multiplexer #(.select(3), .width(8), .enable("false")) multiplexer_1 (
    .in0(add8_1_s), .in1(and8_1_s), .in2(or8_1_s), .in3(nand8_1_s), .in4(nor8_1_s), .in5(xor8_1_s),
    .in6(nxor8_1_s), .in7(not8_1_s), .out(S), .sel(OP_A_EFFECTUER));
endmodule
